# Fritzing sketch System Design (saved by Fritzing 1.0.4)
breadboards: 1

parts:
  Rasp_Pi = Raspberry Pi 4B
  TB6612 = Motor Driver 1A Dual TB6612FNG
  VCC = DC Power [voltage=12V internal_resistance=0.1Ω]
  M1 = DC Motor [voltage_(max)=6V voltage_(min)=3V]
  LM2596 = RioRand LM2596
  M2 = DC Motor [voltage_(max)=6V voltage_(min)=3V]
  I2C_Level_Shifter = PCA9306 [package=psop-8]
  J1 = Basic Servo
  I2C_Level_Shifter1 = PCA9306 [package=psop-8]
  J2 = Basic Servo
  I2C_Level_Shifter2 = PCA9306 [package=psop-8]
  J3 = Basic Servo
  I2C_Level_Shifter3 = PCA9306 [package=psop-8]
  J4 = Basic Servo
  I2C_Level_Shifter4 = PCA9306 [package=psop-8]
  J5 = Basic Servo
  I2C_Level_Shifter5 = PCA9306 [package=psop-8]
  J6 = Basic Servo
  I2C_Level_Shifter6 = PCA9306 [package=psop-8]
  J7 = Basic Servo

nets:
  N1: Rasp_Pi.3V3, TB6612.STBY, I2C_Level_Shifter.VREF1, I2C_Level_Shifter.EN, I2C_Level_Shifter1.VREF1, I2C_Level_Shifter1.EN, I2C_Level_Shifter2.VREF1, I2C_Level_Shifter2.EN, I2C_Level_Shifter3.VREF1, I2C_Level_Shifter3.EN, I2C_Level_Shifter4.VREF1, I2C_Level_Shifter4.EN, I2C_Level_Shifter5.VREF1, I2C_Level_Shifter5.EN, I2C_Level_Shifter6.VREF1, I2C_Level_Shifter6.EN
  N2: Rasp_Pi.GPIO2, I2C_Level_Shifter.SCL1, I2C_Level_Shifter1.SCL1, I2C_Level_Shifter2.SCL1, I2C_Level_Shifter3.SCL1, I2C_Level_Shifter4.SCL1, I2C_Level_Shifter5.SCL1, I2C_Level_Shifter6.SCL1
  N3: Rasp_Pi.GPIO3, I2C_Level_Shifter.SDA1, I2C_Level_Shifter1.SDA1, I2C_Level_Shifter2.SDA1, I2C_Level_Shifter3.SDA1, I2C_Level_Shifter4.SDA1, I2C_Level_Shifter5.SDA1, I2C_Level_Shifter6.SDA1
  N4: Rasp_Pi.GPIO14, TB6612.BIN2
  N5: Rasp_Pi.GPIO15, TB6612.BIN1
  N6: Rasp_Pi.GPIO17, TB6612.PWMB
  N7: Rasp_Pi.GPIO23, TB6612.AIN1
  N8: Rasp_Pi.GPIO24, TB6612.AIN2
  N9: Rasp_Pi.GPIO25, TB6612.PWMA
  GND: Rasp_Pi.GND, TB6612.GND, VCC.V-, LM2596.Pin_2, LM2596.Pin_4, I2C_Level_Shifter.GND, I2C_Level_Shifter1.GND, I2C_Level_Shifter2.GND, I2C_Level_Shifter3.GND, I2C_Level_Shifter4.GND, I2C_Level_Shifter5.GND, I2C_Level_Shifter6.GND
  N10: TB6612.B01, M2.pin_1
  N11: TB6612.B02, M2.pin_2
  N12: TB6612.A02, M1.pin_2
  N13: TB6612.A01, M1.pin_1
  N14: TB6612.VCC, LM2596.Pin_3
  N15: TB6612.VM, VCC.V+, LM2596.Pin_1
  N16: I2C_Level_Shifter.SDA2, J1.gnd
  N17: I2C_Level_Shifter.SCL2, J1.pulse
  N18: I2C_Level_Shifter.VREF2, J1.vcc
  N19: I2C_Level_Shifter1.SDA2, J2.gnd
  N20: I2C_Level_Shifter1.SCL2, J2.pulse
  N21: I2C_Level_Shifter1.VREF2, J2.vcc
  N22: I2C_Level_Shifter2.SDA2, J3.gnd
  N23: I2C_Level_Shifter2.SCL2, J3.pulse
  N24: I2C_Level_Shifter2.VREF2, J3.vcc
  N25: I2C_Level_Shifter3.SDA2, J4.gnd
  N26: I2C_Level_Shifter3.SCL2, J4.pulse
  N27: I2C_Level_Shifter3.VREF2, J4.vcc
  N28: I2C_Level_Shifter4.SDA2, J5.gnd
  N29: I2C_Level_Shifter4.SCL2, J5.pulse
  N30: I2C_Level_Shifter4.VREF2, J5.vcc
  N31: I2C_Level_Shifter5.SDA2, J6.gnd
  N32: I2C_Level_Shifter5.SCL2, J6.pulse
  N33: I2C_Level_Shifter5.VREF2, J6.vcc
  N34: I2C_Level_Shifter6.SDA2, J7.gnd
  N35: I2C_Level_Shifter6.SCL2, J7.pulse
  N36: I2C_Level_Shifter6.VREF2, J7.vcc

notes:
  Single Motor Driver Circuit
